# Fritzing sketch Esquematico (saved by Fritzing 0.9.3b)
circuit board: 4cm x 4.9568cm
breadboards: 1

parts:
  ESP-01 = ESP8266 WiFi Module [part_number=ESP8266]
  BMP280 = BMP280 Breakout Board [part_number=BMP280]
  DHT1 = DHT11 Humitidy and Temperature Sensor
  VCC = screw terminal, 2 pins
  R1 = Resistor [tolerance=±5% resistance=3.3k package=THT]
  R2 = Resistor [tolerance=±5% resistance=3.3k package=THT]
  C1 = Electrolytic Capacitor [capacitance=100μF package="100 mil [THT, electrolytic]"]

nets:
  VCC: ESP-01.VCC, BMP280.VCC, BMP280.SDO, DHT1.VDD, VCC.pin2, R1.Pin_0, R2.Pin_0, C1.+
  N1: ESP-01.GPIO_0, BMP280.SDA
  N2: ESP-01.RST, R1.Pin_1
  N3: ESP-01.GPIO_2, BMP280.SCL
  N4: ESP-01.CH_PD, R2.Pin_1
  GND: ESP-01.GND, BMP280.GND, DHT1.GND, VCC.pin1, C1.-
  N5: ESP-01.TXD, DHT1.DATA

notes:
  GND

custom parts:
  ESP8266 WiFi Module: Generic WiFi Module based on the ESP8266 with onboard PCB antenna and UART communications
  BMP280 Breakout Board: This is a breakout board for the Bosch Sensortec BMP280, "an absolute barometric pressure sensor especially designed for mobile applications." The operation range is 300 to 1100 hPa. Supply voltage is 1.2 to 3.6V. Operating temperature range is -40 to +85 °C.
  DHT11 Humitidy and Temperature Sensor: DHT11 Humidity and Temperature Sensor
